# Fritzing sketch 7segment4digitDisplay (saved by Fritzing 0.9.3b)
breadboards: 1

parts:
  7_Segment_4_Digit_Display1 = 7-SEGMENT-4DIGIT common cathode [part_number=HS420561K-32 package=7-segment-4digit-cathode]
  Part1 = Arduino Uno (Rev3)
  R1 = Resistor [tolerance=±5% resistance=330 package=THT]
  R2 = Resistor [tolerance=±5% resistance=330 package=THT]
  R3 = Resistor [tolerance=±5% resistance=330 package=THT]
  R4 = Resistor [tolerance=±5% resistance=330 package=THT]
  R5 = Resistor [tolerance=±5% resistance=330 package=THT]
  R6 = Resistor [tolerance=±5% resistance=330 package=THT]
  R7 = Resistor [tolerance=±5% resistance=330 package=THT]
  R8 = Resistor [tolerance=±5% resistance=330 package=THT]

nets:
  N1: 7_Segment_4_Digit_Display1.pin_1, R1.Pin_1
  N2: 7_Segment_4_Digit_Display1.pin_2, R3.Pin_1
  N3: 7_Segment_4_Digit_Display1.pin_3, R2.Pin_1
  N4: 7_Segment_4_Digit_Display1.pin_4, R4.Pin_0
  N5: 7_Segment_4_Digit_Display1.pin_5, R5.Pin_0
  N6: 7_Segment_4_Digit_Display1.pin_6, Part1.D6_PWM
  N7: 7_Segment_4_Digit_Display1.pin_7, R8.Pin_0
  N8: 7_Segment_4_Digit_Display1.pin_8, Part1.D8
  N9: 7_Segment_4_Digit_Display1.pin_9, Part1.D9_PWM
  N10: 7_Segment_4_Digit_Display1.pin_10, R7.Pin_1
  N11: 7_Segment_4_Digit_Display1.pin_11, R6.Pin_1
  N12: 7_Segment_4_Digit_Display1.pin_12, Part1.D12/MISO
  N13: Part1.D10_PWM/SS, R7.Pin_0
  N14: Part1.D11_PWM/MOSI, R6.Pin_0
  N15: Part1.D1/TX, R1.Pin_0
  N16: Part1.D2, R3.Pin_0
  N17: Part1.D3_PWM, R2.Pin_0
  N18: Part1.D4, R4.Pin_1
  N19: Part1.D5_PWM, R5.Pin_1
  N20: Part1.D7, R8.Pin_1

custom parts:
  7-SEGMENT-4DIGIT common cathode: A 7 Segment 4 Digit common cathode display, with decimal points
