# Fritzing sketch simple-alarm-clock (saved by Fritzing 0.9.3b)
breadboards: 1

parts:
  7_Segment_4_Digit_Display1 = 7-SEGMENT-4DIGIT common cathode [part_number=HS420561K-32 package=7-segment-4digit-cathode]
  Part1 = Arduino Uno (Rev3)
  R1 = Resistor [tolerance=±5% resistance=330 package=THT]
  R2 = Resistor [tolerance=±5% resistance=330 package=THT]
  R3 = Resistor [tolerance=±5% resistance=330 package=THT]
  R4 = Resistor [tolerance=±5% resistance=330 package=THT]
  R5 = Resistor [tolerance=±5% resistance=330 package=THT]
  R6 = Resistor [tolerance=±5% resistance=330 package=THT]
  R7 = Resistor [tolerance=±5% resistance=330 package=THT]
  R8 = Resistor [tolerance=±5% resistance=330 package=THT]
  Part2 = Shift Register Breakout - 74HC595
  Part3 = Real Time Clock Module - DS1307 RTC Breakout Board
  J1 = Piezo Speaker  # not connected
  S1 = Pushbutton [package="[THT]"]  # not connected
  S2 = Pushbutton [package="[THT]"]  # not connected
  S3 = Pushbutton [package="[THT]"]  # not connected
  S4 = Pushbutton [package="[THT]"]  # not connected
  S5 = Pushbutton [package="[THT]"]  # not connected
  LED1 = LED - 5mm [color="Red (633nm)" package="5 mm [THT]"]  # not connected

nets:
  N1: 7_Segment_4_Digit_Display1.pin_1, R6.Pin_0
  N2: 7_Segment_4_Digit_Display1.pin_2, R8.Pin_0
  N3: 7_Segment_4_Digit_Display1.pin_3, R7.Pin_0
  N4: 7_Segment_4_Digit_Display1.pin_4, R5.Pin_0
  N5: 7_Segment_4_Digit_Display1.pin_5, R4.Pin_0
  N6: 7_Segment_4_Digit_Display1.pin_6, Part1.D4
  N7: 7_Segment_4_Digit_Display1.pin_7, R2.Pin_1
  N8: 7_Segment_4_Digit_Display1.pin_8, Part1.D3_PWM
  N9: 7_Segment_4_Digit_Display1.pin_9, Part1.D2
  N10: 7_Segment_4_Digit_Display1.pin_10, R1.Pin_0
  N11: 7_Segment_4_Digit_Display1.pin_11, R3.Pin_0
  N12: 7_Segment_4_Digit_Display1.pin_12, Part1.D1/TX
  N13: Part1.A4/SDA, Part3.SQW
  N14: Part1.A5/SCL, Part3.SCL
  N15: Part1.D8, Part2.SERIAL_IN
  N16: Part1.D6_PWM, Part2.CLOCK
  N17: Part1.D7, Part2.LATCH_CLOCK
  5V: Part1.5V, Part2.VCC
  GND: Part1.GND, Part2.GND
  N18: R1.Pin_1, Part2.QF
  N19: R2.Pin_0, Part2.QB
  N20: R3.Pin_1, Part2.QA
  N21: R4.Pin_1, Part2.QG
  N22: R5.Pin_1, Part2.QC
  N23: R6.Pin_1, Part2.QE
  N24: R7.Pin_1, Part2.QH
  N25: R8.Pin_1, Part2.QD

custom parts:
  7-SEGMENT-4DIGIT common cathode: A 7 Segment 4 Digit common cathode display, with decimal points
