# Fritzing sketch temperatureClock (saved by Fritzing 0.9.3b)
breadboards: 1

parts:
  7_Segment_4_Digit_Display1 = 7-SEGMENT-4DIGIT common cathode [part_number=HS420561K-32 package=7-segment-4digit-cathode]
  Part1 = Arduino Uno (Rev3)
  R1 = Resistor [tolerance=±5% resistance=330 package=THT]
  R2 = Resistor [tolerance=±5% resistance=330 package=THT]
  R3 = Resistor [tolerance=±5% resistance=330 package=THT]
  R4 = Resistor [tolerance=±5% resistance=330 package=THT]
  R5 = Resistor [tolerance=±5% resistance=330 package=THT]
  R6 = Resistor [tolerance=±5% resistance=330 package=THT]
  R7 = Resistor [tolerance=±5% resistance=330 package=THT]
  R8 = Resistor [tolerance=±5% resistance=330 package=THT]
  Part2 = Shift Register Breakout - 74HC595
  Part3 = Real Time Clock Module - DS1307 RTC Breakout Board
  BMP180_Breakout1 = Barometric Pressure Sensor - BMP180 Breakout (GY-68)
  S1 = Pushbutton [package="[THT]"]
  R9 = Resistor [tolerance=±5% resistance=1M package=THT]
  LED1 = LED - 5mm [color="Red (633nm)" package="5 mm [THT]"]
  R10 = Resistor [tolerance=±5% resistance=220 package=THT]

nets:
  N1: 7_Segment_4_Digit_Display1.pin_1, R6.Pin_0
  N2: 7_Segment_4_Digit_Display1.pin_2, R8.Pin_0
  N3: 7_Segment_4_Digit_Display1.pin_3, R7.Pin_0
  N4: 7_Segment_4_Digit_Display1.pin_4, R5.Pin_0
  N5: 7_Segment_4_Digit_Display1.pin_5, R4.Pin_0
  N6: 7_Segment_4_Digit_Display1.pin_6, Part1.D5_PWM
  N7: 7_Segment_4_Digit_Display1.pin_7, R2.Pin_1
  N8: 7_Segment_4_Digit_Display1.pin_8, Part1.D4
  N9: 7_Segment_4_Digit_Display1.pin_9, Part1.D3_PWM
  N10: 7_Segment_4_Digit_Display1.pin_10, R1.Pin_0
  N11: 7_Segment_4_Digit_Display1.pin_11, R3.Pin_0
  N12: 7_Segment_4_Digit_Display1.pin_12, Part1.D2
  N13: Part1.A0, LED1.anode
  N14: Part1.A4/SDA, Part3.SQW, BMP180_Breakout1.GND
  N15: Part1.A5/SCL, Part3.SCL, BMP180_Breakout1.VCC
  N16: Part1.D8, Part2.SERIAL_IN
  N17: Part1.D9_PWM, S1.Pin_3, S1.Pin_4, R9.Pin_1
  N18: Part1.D6_PWM, Part2.CLOCK
  N19: Part1.D7, Part2.LATCH_CLOCK
  5V: Part1.5V, Part2.VCC
  GND: Part1.GND, Part2.GND
  N20: R1.Pin_1, Part2.QF
  N21: R2.Pin_0, Part2.QB
  N22: R3.Pin_1, Part2.QA
  N23: R4.Pin_1, Part2.QG
  N24: R5.Pin_1, Part2.QC
  N25: R6.Pin_1, Part2.QE
  N26: R7.Pin_1, Part2.QH
  N27: R8.Pin_1, Part2.QD
  N28: S1.Pin_1, S1.Pin_2
  N29: R9.Pin_0, R10.Pin_0
  N30: LED1.cathode, R10.Pin_1

custom parts:
  7-SEGMENT-4DIGIT common cathode: A 7 Segment 4 Digit common cathode display, with decimal points
