# Fritzing sketch tiny-rtc (saved by Fritzing 0.9.3b)
breadboards: 1

parts:
  Part1 = Arduino Uno (Rev3)
  Part2 = Real Time Clock Module - DS1307 RTC Breakout Board

nets:
  N1: Part1.A4/SDA, Part2.SQW
  N2: Part1.A5/SCL, Part2.SCL
  5V: Part1.5V, Part2.5V
  GND: Part1.GND, Part2.GND
