# Fritzing sketch turn-on-light (saved by Fritzing 0.9.3b)
breadboards: 1

parts:
  Part1 = Arduino Uno (Rev3)
  S1 = Pushbutton [package="[THT]"]
  R2 = Resistor [tolerance=±5% resistance=220 package=THT]
  LED1 = LED - 5mm [color="Red (633nm)" package="5 mm [THT]"]  # not connected
  R3 = Resistor [tolerance=±5% resistance=220 package=THT]

nets:
  N1: Part1.D1/TX, R2.Pin_1
  N2: Part1.D2, S1.Pin_3, S1.Pin_4, R3.Pin_1
  N3: Part1.5V, S1.Pin_1, S1.Pin_2
  N4: Part1.GND, R3.Pin_0
